# Fritzing sketch googlebike (saved by Fritzing 0.4.3b)
breadboards: 1

parts:
  Cadence_Sensor = Reed switch [package=THT]
  Joystick_HORZ = Rotary Potentiometer (Small)
  Joystick_VERT = Rotary Potentiometer (Small)
  Joystick_SEL = Pushbutton [package="[THT]"]
  Arduino = Arduino

nets:
  GND: Cadence_Sensor.pin_1, Joystick_HORZ.leg1, Joystick_VERT.leg1, Joystick_SEL.Pin_3, Joystick_SEL.Pin_4
  N1: Cadence_Sensor.pin_2, Arduino.D3
  N2: Joystick_HORZ.wiper, Arduino.A1
  5V: Joystick_HORZ.leg2, Joystick_VERT.leg2
  N3: Joystick_VERT.wiper, Arduino.A0
  N4: Joystick_SEL.Pin_1, Arduino.D2
